# Fritzing sketch IR.Emitter-Receiver (saved by Fritzing 0.9.2b)
circuit board: 4.5cm x 1.4cm
breadboards: 1

parts:
  PART1 = SparkFun Block for Intel Edison - GPIO [part_number=DEV-13038]
  C2 = Electrolytic Capacitor [capacitance=100μF package="100 mil [THT, electrolytic]"]
  IR1 = TSOP312.., 314.. [package=THT]
  R2 = Resistor [tolerance=±5% resistance=1k package=THT]
  R3 = Resistor [tolerance=±5% resistance=330 package=THT]
  R4 = Resistor [tolerance=±5% resistance=33 package=THT]
  LED1 = LED - 5mm [color="Red (633nm)" package="5 mm [THT]"]

nets:
  N1: PART1.GP13, R4.Pin_0
  GND: PART1.GND, C2.-, IR1.GND, LED1.cathode
  N2: PART1.VSYS, R2.Pin_1, R3.Pin_1
  N3: PART1.GP44, IR1.Data, R2.Pin_0
  N4: C2.+, IR1.Vs, R3.Pin_0
  N5: R4.Pin_1, LED1.anode

custom parts:
  SparkFun Block for Intel Edison - GPIO: The Intel® Edison is an ultra small computing platform that will change the way you look at embedded electronics. Each Edison is packed with a huge amount of tech goodies into a tiny package while still providing the same robust strength of your go-to single board computer. Powered by the Intel® Atom™ SoC dual-core CPU and including an integrated WiFi, Bluetooth LE, and a 70-pin connector to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
  TSOP312.., 314..: The TSOP312.., TSOP314.. series are miniaturized receivers for infrared remote control systems. A PIN diode and a preamplifier are assembled on a lead frame, the epoxy package acts as an IR filter. The demodulated output signal can be directly decoded by a microprocessor. The TSOP312.. is compatible with all common IR remote control data formats. The TSOP314.. is optimized to suppress almost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
