# Fritzing sketch IR.Emitter (saved by Fritzing 0.9.2b)
circuit board: 3.5cm x 1.4cm
breadboards: 1

parts:
  PART1 = SparkFun Block for Intel Edison - GPIO [part_number=DEV-13038]
  R1 = Resistor [tolerance=±5% resistance=33 package=THT]
  LED = LED - 3mm [color="Red (633nm)" package="3 mm [THT]"]

nets:
  N1: PART1.GP13, R1.Pin_0
  N2: PART1.GND, LED.cathode
  N3: R1.Pin_1, LED.anode

custom parts:
  SparkFun Block for Intel Edison - GPIO: The Intel® Edison is an ultra small computing platform that will change the way you look at embedded electronics. Each Edison is packed with a huge amount of tech goodies into a tiny package while still providing the same robust strength of your go-to single board computer. Powered by the Intel® Atom™ SoC dual-core CPU and including an integrated WiFi, Bluetooth LE, and a 70-pin connector to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
